# Fritzing sketch greenHouse (saved by Fritzing 0.9.3b)

parts:
  Часть1 = Soil Moisture Sensor  # not connected
  Часть2 = Arduino Nano (Rev3.0)
  LED1 = LEDs [package=led10mm]
  Part3 = Lilypad Battery Connect
  Mod1 = generic-ac-power-supply [package=THT]  # not connected
  JP1 = LITTLEBITS_FEMALE [package=little_bits_female]  # not connected
  JP2 = Header 2 [package=molex-1x2_lock]  # not connected
  KY-1 = Keyes Relay [package=THT]
  J1 = HANRUN RJ-45 [package=hanrun]  # not connected
  Part4 = Lilypad Battery Connect
  JP3 = Header 6 [package=molex-1x6_lock]  # not connected
  Часть3 = Lilypad Battery Connect
  R1 = RPACK* [package=rpack-sip-pth-5]
  R2 = RPACK* [package=rpack-sip-pth-5]

nets:
  N1: Часть2.D8, KY-1.signal
  N2: Часть2.VIN, Part4.+
  N3: Часть2.GND, Part4.-
  N4: LED1.A, Part3.+
  N5: LED1.C, KY-1.NO
  N6: Part3.-, KY-1.C
  N7: KY-1.power, R1.2
  N8: KY-1.ground, R2.2
  N9: Часть3.-, R2.1
  N10: Часть3.+, R1.1

notes:
  240V AC power supply
  12 DC power supply
  Light Sensor
  5 DC
  Power Supply

custom parts:
  LEDs: LEDs Standard schematic elements and footprints for 5mm, 3mm, 1206, and 0603 sized LEDs. 5mm - Spark Fun Electronics SKU : COM-00529 (and others)
  generic-ac-power-supply: Generic ac power supply module. Use as is, or customize the svgs to fit your particular device (as they are all different.) Provides AC input and single DC output. PCB is generic and will need modifications if you intend to do a pcb mount.
  Keyes Relay: The Keyes 5V relay module is suitable for SCM development, home appliance control. It uses a 5V~12V TIL control signal which can control DC / AC signal.
  HANRUN RJ-45: RJ-45 with LEDs HANRUN HR911105A
